# Fritzing sketch depth-repeater-board (saved by Fritzing 0.9.3b)
stripboards: 1

parts:
  Nano1 = Arduino Nano v2.3
  U1 = MAX485 [package=dil08]
  J1 = Camdenboss CTB0158-2 [part_number=CTB0158-2 package=THT]
  J2 = Camdenboss CTB0158-2 [part_number=CTB0158-2 package=THT]
  IC1 = Voltage Regulator [package=78xxl]
  J3 = Camdenboss CTB0158-2 [part_number=CTB0158-2 package=THT]

nets:
  N1: Nano1.D0RX, U1.RO
  GND: Nano1.GND, U1.GND, IC1.GND, J3.pin1
  N2: Nano1.D2, U1.RE
  N3: Nano1.D3, J1.pin2
  N4: Nano1.D12, J1.pin1
  +5V: Nano1.+5V, U1.VCC, IC1.OUT
  N5: U1.A, J2.pin1
  N6: U1.B, J2.pin2
  N7: IC1.IN, J3.pin2
